# Fritzing sketch motor_controller (saved by Fritzing 0.9.4)
breadboards: 2

parts:
  Part1 = Arduino Mega ADK (Rev3)
  Part4 = Adafruit Motor/Stepper/Servo Shield [part_number="Adafruit #1438"]
  HC-SR04_Sensor_1 = HC-SR04 Ultrasonic Distance Sensor
  Part5 = InvenSense MPU6050
  Part6 = BlueSMiRF Silver [part_number=10269]
  VCC1 = Battery
  LED1 = LED - 3mm [color="Yellow (595nm)" package="3 mm [THT]"]
  LED2 = LED - 3mm [color="Green (555nm)" package="3 mm [THT]"]
  LED3 = LED - 3mm [color="Red (633nm)" package="3 mm [THT]"]
  R1 = Resistor [tolerance=±5% resistance=220 package="2010 [SMD]"]
  R2 = Resistor [tolerance=±5% resistance=220 package="2010 [SMD]"]
  R3 = Resistor [tolerance=±5% resistance=220 package="2010 [SMD]"]
  Part7 = Adafruit 4-channel I2C-safe Bi-directional Logic Level Converter [part_number="Adafruit #757"]
  MCU1 = Raspberry Pi Zero  # not connected

nets:
  N1: Part1.D19/RX1, Part6.TX_5V
  N2: Part1.D18/TX1, Part6.RX_5V
  N3: Part1.D22, HC-SR04_Sensor_1.TRIG
  N4: Part1.D23, HC-SR04_Sensor_1.ECHO
  N5: Part1.D44, LED3.anode
  N6: Part1.D46, LED2.anode
  N7: Part1.D48, LED1.anode
  GND: Part4.GND, HC-SR04_Sensor_1.GND, Part5.GND, Part6.GND, VCC1.-, R1.Pin_1, R2.Pin_1, R3.Pin_1, Part7.GND
  N8: Part4.VMOTOR, VCC1.+
  VCC: Part4.+5V, HC-SR04_Sensor_1.VCC, Part5.VCC, Part6.VCC, Part7.HV
  N9: Part4.D2, Part5.INT
  N10: Part4.AD5/SCL, Part5.SCL
  N11: Part4.AD4/SDA, Part5.SDA
  N12: LED1.cathode, R1.Pin_0
  N13: LED2.cathode, R2.Pin_0
  N14: LED3.cathode, R3.Pin_0

custom parts:
  Adafruit Motor/Stepper/Servo Shield: The original Adafruit Motorshield kit is one of our most beloved kits, which is why we decided to make something even better. We have upgraded the shield kit to make the bestest, easiest way to drive DC and Stepper motors. This shield will make quick work of your next robotics project! We kept the ability to drive up to 4 DC motors or 2 stepper motors, but added many improvements: Instead of a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
  HC-SR04 Ultrasonic Distance Sensor: The HC-SR04 is an ultrasonic distance sensor. It is capable of providing measurement for ranges of 2cm to 400cm. The module operates at 5V.
  BlueSMiRF Silver: Description: The BlueSMiRF Silver is the latest Bluetooth wireless serial cable replacement from SparkFun Electronics! This version of the popular BlueSMiRF uses the RN-42 module which has a bit less range than the RN-41 module used in the BlueSMiRF Gold. These modems work as a serial (RX/TX) pipe. Any serial stream from 2400 to 115200bps can be passed seamlessly from your computer to your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
  Battery: Your standard 2x 18650 battery pack (7,4 Volts)
  Adafruit 4-channel I2C-safe Bi-directional Logic Level Converter: Because the Arduino (and Basic Stamp) are 5V devices, and most modern sensors, displays, flash cards and modes are 3.3V-only, many makers find that they need to perform level shifting/conversion to protect the 3.3V device from 5V. We do have some other handy level shifters in the shop, from the DIP 74LVC245 to the fancy bi-directional TXB0108. However, neither of these are happy to work with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
